# Fritzing sketch sketch (saved by Fritzing 0.9.2b)
circuit board: 8.46667cm x 5.64444cm
breadboards: 1

parts:
  R3 = Resistor [tolerance=±5% resistance=100 package=THT]
  Q1 = Basic FET N-Channel [package="TO220 [THT]"]
  Q2 = Basic FET N-Channel [package="TO220 [THT]"]
  Q3 = Basic FET N-Channel [package="TO220 [THT]"]
  R2 = Resistor [tolerance=±5% resistance=100 package=THT]
  R1 = Resistor [tolerance=±5% resistance=100 package=THT]
  ArduinoUno = Arduino Uno (Rev3)

nets:
  N1: R3.Pin_0, ArduinoUno.D3_PWM
  N2: R3.Pin_1, Q3.gate
  N3: Q1.gate, R1.Pin_1
  N4: Q1.source, Q2.source, Q3.source, ArduinoUno.GND
  N5: Q2.gate, R2.Pin_1
  N6: R2.Pin_0, ArduinoUno.D6_PWM
  N7: R1.Pin_0, ArduinoUno.D5_PWM

notes:
  12V power supply
  +12V
  red
  green
  blue
  LED Strip
